// Logisim project Masina2.circ as structural Verilog: 1 circuit, main circuit main
module main (
  input  X1,
  input  X2,
  output Lampica
);

  wire A_A_out, A_B_out, A_C_out, A_D_out, B_A_out, B_B_out, B_C_out, B_D_out, C_A_out, C_B_out, C_D_out,
       clock_1_out, D_A_out, D_B_out, D_C_out, E_A_out, E_B_out, E_C_out, E_D_out, Q2_q;

  nand B_A (B_A_out, X2, X2);
  nand B_B (B_B_out, Lampica, Lampica);
  nand C_A (C_A_out, Q2_q, Q2_q);
  Clock clock_1 (.out(clock_1_out));
  nand E_C (E_C_out, Q2_q, Lampica);
  D_Flip_Flop Q1 (.D(A_B_out), .clk(clock_1_out), .Q(Lampica));  // open: Qn, preset, reset
  D_Flip_Flop Q2 (.D(E_D_out), .clk(clock_1_out), .Q(Q2_q));  // open: Qn, preset, reset
  nand A_A (A_A_out, X1, B_B_out);
  nand A_C (A_C_out, X2, B_B_out);
  nand A_D (A_D_out, A_C_out, A_C_out);
  nand B_C (B_C_out, A_D_out, Q2_q);
  nand B_D (B_D_out, X2, B_B_out);
  nand D_A (D_A_out, B_A_out, B_B_out);
  nand C_B (C_B_out, B_D_out, B_D_out);
  nand C_D (C_D_out, C_B_out, C_A_out);
  nand D_B (D_B_out, D_A_out, D_A_out);
  nand A_B (A_B_out, A_A_out, B_C_out);
  nand E_A (E_A_out, C_D_out, D_C_out);
  nand D_C (D_C_out, D_B_out, Q2_q);
  nand E_B (E_B_out, E_A_out, E_A_out);
  nand E_D (E_D_out, E_B_out, E_C_out);
endmodule
